// Logisim project 7_SEGMENT_DISPLAY.circ as structural Verilog: 1 circuit, main circuit main
module main (
  input  A,
  input  B,
  input  C,
  input  D
);

  wire and_1_out, and_2_out, and_3_out, and_4_out, and_5_out, and_6_out, and_7_out, and_8_out, not_1_out,
       not_2_out, not_4_out, not_5_out, or_1_out, or_2_out, or_3_out, or_4_out, or_5_out, or_6_out, or_7_out,
       or_8_out, or_9_out, or_10_out, or_11_out, or_12_out, xnor_1_out, xnor_2_out;

  not not_1 (not_1_out, A);
  not not_2 (not_2_out, B);
  not not_3 (not_2_out, B);
  not not_4 (not_4_out, C);
  not not_5 (not_5_out, D);
  or or_1 (or_1_out, A, C);
  xnor xnor_1 (xnor_1_out, B, D);
  xnor xnor_2 (xnor_2_out, C, D);
  or or_2 (or_2_out, not_2_out, C);
  or or_3 (or_3_out, not_2_out, C);
  or or_4 (or_4_out, B, not_4_out);
  or or_5 (or_5_out, not_2_out, not_5_out);
  and and_1 (and_1_out, or_2_out, not_5_out);
  and and_2 (and_2_out, not_2_out, C);
  and and_3 (and_3_out, B, not_4_out, D);
  and and_4 (and_4_out, or_4_out, not_5_out);
  and and_5 (and_5_out, B, not_4_out);
  and and_6 (and_6_out, or_5_out, C);
  and and_7 (and_7_out, B, not_4_out);
  or or_6 (or_6_out, or_1_out, xnor_1_out);
  or or_7 (or_7_out, xnor_2_out, not_2_out);
  or or_8 (or_8_out, B, not_4_out, D);
  and and_8 (and_8_out, or_3_out, not_5_out);
  or or_9 (or_9_out, and_1_out, A);
  or or_10 (or_10_out, or_9_out, and_2_out, and_3_out);
  or or_11 (or_11_out, and_4_out, and_5_out, A);
  or or_12 (or_12_out, and_6_out, and_7_out, A);
  _7_Segment_Display u_7_segment_display_1 (
    .g(or_12_out), .f(or_11_out), .a(or_6_out), .b(or_7_out), .e(and_8_out), .d(or_10_out), .c(or_8_out));  // open: dp
endmodule
